# Fritzing sketch Arduboy (saved by Fritzing 0.9.3b)
breadboards: 1

parts:
  S4 = Pushbutton [package="[THT]"]
  Part1 = Arduino Uno (Rev3)
  S5 = Pushbutton [package="[THT]"]
  S6 = Pushbutton [package="[THT]"]
  S7 = Pushbutton [package="[THT]"]
  Nokia_5110_LCD_Module1 = Nokia 5110 LCD basado en PCD8544
  R1 = Resistor [tolerance=±5% resistance=220 package=THT]

nets:
  N1: S4.Pin_1, S4.Pin_2, Part1.5V, Nokia_5110_LCD_Module1.LIGHT
  N2: S4.Pin_3, S4.Pin_4, Part1.D2
  N3: Part1.D10_PWM/SS, R1.Pin_1
  N4: Part1.D11_PWM/MOSI, S7.Pin_3, S7.Pin_4
  N5: Part1.D12/MISO, S6.Pin_1, S6.Pin_2
  N6: Part1.D3_PWM, S5.Pin_1, S5.Pin_2
  GND: Part1.GND, S5.Pin_3, S5.Pin_4, S6.Pin_3, S6.Pin_4, S7.Pin_1, S7.Pin_2, Nokia_5110_LCD_Module1.GND

custom parts:
  Nokia 5110 LCD basado en PCD8544: Módulo Nokia 5110 LCD basado en el controlador PCD8544. Versión de 8 pines (sólo entrada).
